# Fritzing sketch Untitled Sketch 2 (saved by Fritzing 0.9.2b)
breadboards: 1

parts:
  R1 = Resistor [tolerance=±5% resistance=220 package=THT]
  Raspberry_Pi1 = Raspberry Pi 2
  T1 = LM35 Temperature Sensor [thermistor_type=NTC package="TO92 [THT]"]  # not connected

nets:
  N1: R1.Pin_0, Raspberry_Pi1.GIPO4
  N2: R1.Pin_1, Raspberry_Pi1.3v3
