# Fritzing sketch temparatur (saved by Fritzing 0.9.2b)
breadboards: 1

parts:
  Raspberry_Pi1 = Raspberry Pi 2
  T1 = LM35 Temperature Sensor [thermistor_type=NTC package="TO92 [THT]"]  # not connected
  R1 = Resistor [tolerance=±5% resistance=4.7k package=THT]

nets:
  N1: Raspberry_Pi1.3v3, R1.Pin_1
  N2: Raspberry_Pi1.GIPO4, R1.Pin_0
