# Fritzing sketch ampel (saved by Fritzing 0.9.0b)
breadboards: 1

parts:
  LED1 = LED - 5mm [color="Red (633nm)" package="5 mm [THT]"]
  LED2 = LED - 5mm [color="Yellow (595nm)" package="5 mm [THT]"]
  LED3 = LED - 5mm [color="Green (560nm)" package="5 mm [THT]"]
  Raspberry_Pi1 = Raspberry Pi B+
  R1 = Resistor [tolerance=±10% resistance=300 package=THT]

nets:
  N1: LED1.cathode, LED2.cathode, LED3.cathode, R1.Pin_1
  N2: LED1.anode, Raspberry_Pi1.GIPO22
  N3: LED2.anode, Raspberry_Pi1.GIPO10
  N4: LED3.anode, Raspberry_Pi1.GIPO11
  N5: Raspberry_Pi1.GND, R1.Pin_0
