# Fritzing sketch eine_led (saved by Fritzing 0.9.0b)
breadboards: 1

parts:
  LED4 = LED - 5mm [color="Red (633nm)" package="5 mm [THT]"]
  Raspberry_Pi2 = Raspberry Pi B+
  R1 = Resistor [tolerance=±20% resistance=300 package=THT]

nets:
  N1: LED4.cathode, R1.Pin_1
  N2: LED4.anode, Raspberry_Pi2.GIPO22
  N3: Raspberry_Pi2.GND, R1.Pin_0
